// Digital circuit mainBus.dig as structural Verilog
module mainBus (
  input  clk
);

  wire ACC_e, ADDRRam_e, ALU_CYin, ALU_INV, ALU_OUTe, ALU_RSLTe, ALU_SUB, DIRECTAddr_e, IO_e, IORD_e, IOWR_e,
       not_1_out, NXT_I, or_1_out, PCCNT_e, PCLD_e, PCOUT_e, RAM_e, RAMRD_e, RAMWR_e, RInst_E, RST, WR_nRD_e;
  wire [2:0] counter_1_out;
  wire [3:0] PGM_mem_d;
  wire [7:0] _5bitpc2_1_pc_out, Acc_W_q_x, ALU_dsp, PGM_mem_d_2, Reg_I_2_q_x, Reg_I_q_x;

  or or_1 (or_1_out, RST, NXT_I);
  LED led_1 ();  // open: in
  LED led_2 ();  // open: in
  Button RESET (.out(RST));
  LED led_3 ();  // open: in
  LED led_4 ();  // open: in
  Counter #(.Bits(3)) counter_1 (.en(1'b1), .C(clk), .clr(or_1_out), .out(counter_1_out));  // open: ovf
  LED led_5 ();  // open: in
  Seven_Seg_Hex seven_seg_hex_1 (.d({1'b0, counter_1_out}), .dp(1'b0));
  _5bitPC2 _5bitpc2_1 (
    .PC_in(_5bitpc2_1_pc_out), .Le_a(PCLD_e), .CNTe_a(PCCNT_e), .CLK(clk), .CLR(RST), .Re_a(PCOUT_e),
    .PC_out(_5bitpc2_1_pc_out));
  sapRegX Reg_I (.E_in(RInst_E), .D_x(_5bitpc2_1_pc_out), .E_out(1'b1), .Q_x(Reg_I_q_x));
  ROM #(.AddrBits(5), .Bits(12)) PGM_mem (.A(Reg_I_q_x[4:0]), .sel(1'b1), .D({PGM_mem_d_2, PGM_mem_d}));
  assign _5bitpc2_1_pc_out = DIRECTAddr_e ? PGM_mem_d_2 : 8'bz;  // Driver driver_1
  LookUpTable #(.Bits(16)) MicroCodigo (
    .in0(counter_1_out[0]), .in1(counter_1_out[1]), .in2(counter_1_out[2]), .in3(PGM_mem_d[0]),
    .in4(PGM_mem_d[1]), .in5(PGM_mem_d[2]), .in6(PGM_mem_d[3]),
    .out({WR_nRD_e, ALU_CYin, ALU_INV, ALU_SUB, IO_e, RAM_e, ALU_OUTe, ALU_RSLTe, ACC_e, ADDRRam_e, DIRECTAddr_e, RInst_E, NXT_I, PCOUT_e, PCCNT_e, PCLD_e}));
  Seven_Seg_Hex seven_seg_hex_2 (.d(_5bitpc2_1_pc_out[7:4]), .dp(1'b0));
  sapRegX Acc_W (.E_in(ACC_e), .D_x(_5bitpc2_1_pc_out), .E_out(1'b1), .Q_x(Acc_W_q_x));
  sapRegX Reg_I_2 (.E_in(ADDRRam_e), .D_x(_5bitpc2_1_pc_out), .E_out(1'b1), .Q_x(Reg_I_2_q_x));
  not not_1 (not_1_out, WR_nRD_e);
  Seven_Seg_Hex seven_seg_hex_3 (.d(_5bitpc2_1_pc_out[3:0]), .dp(1'b0));
  and and_1 (RAMWR_e, WR_nRD_e, RAM_e);
  and and_2 (RAMRD_e, RAM_e, not_1_out);
  and and_3 (IOWR_e, WR_nRD_e, IO_e);
  and and_4 (IORD_e, IO_e, not_1_out);
  sapALU_1 sapalu_1_1 (.INV(ALU_INV), .CY(ALU_CYin), .A(Acc_W_q_x), .B(_5bitpc2_1_pc_out), .SUB(ALU_SUB));
  RAMSinglePort #(.AddrBits(8), .Bits(8)) ramsingleport_1 (
    .A(Reg_I_2_q_x), .str(RAMWR_e), .C(clk), .ld(RAMRD_e), .D(_5bitpc2_1_pc_out));
  sapRegX Reg_B (.E_in(ALU_RSLTe), .D_x(ALU_dsp), .E_out(ALU_OUTe), .Q_x(_5bitpc2_1_pc_out));
  Seven_Seg_Hex seven_seg_hex_4 (.d(ALU_dsp[7:4]), .dp(1'b0));
  Seven_Seg_Hex seven_seg_hex_5 (.d(ALU_dsp[3:0]), .dp(1'b0));

  // Notes on the sheet:
  //   Formato da instrução
  //   OOOOAAAAAAAA
  //   OOOO -> Codigo de instrucao
  //   AAAAAAAA -->> Endereco do operando / valor
  //   contents of PGM_mem (hex, n*v repeats v):
  //   7*1
  //   contents of MicroCodigo (hex, n*v repeats v):
  //   4*0,28,0,6,0,28,0,5,0,2040,0,10,5*0,50,0,50
  //   256 byte
  //   ScratchPad memory
endmodule
